# Fritzing sketch SpyRobot (saved by Fritzing 0.7.12b)
breadboards: 1

parts:
  IC1 = ULN2003A [package="DIP16 [THT]"]
  Arduino1 = Arduino
  S1 = Toggle Switch [package=THT]
  M3 = DC Motor
  M4 = DC Motor
  VCC1 = 4 x AAA Battery Mount
  VCC2 = Battery block 9V
  R1 = Photocell (LDR) [package=THT]
  R2 = 10k Ω Resistor [package=THT]

nets:
  N1: IC1.In_1, Arduino1.D5
  N2: IC1.In_2, Arduino1.D6
  N3: IC1.0V, Arduino1.GND, VCC1.-, VCC2.-, R1.pin_0
  N4: IC1.COM_-_Common, S1.COM, M3.pin_2, M4.pin_2
  N5: IC1.Out_2, M4.pin_1
  N6: IC1.Out_1, M3.pin_1
  N7: Arduino1.+5V, R2.Pin_1
  N8: Arduino1.VIN, VCC2.+
  N9: Arduino1.A0, R1.pin_1, R2.Pin_0
  N10: S1.L1, VCC1.+
